# Fritzing sketch B737_Overhead_AFT (saved by Fritzing 0.9.10b)
perfboards: 1

parts:
  DM13A = MAX7219 [package=dil24]
  RSC_Master_Board1 = Arduino Mega 2560 (Rev3)
  Mux = Analog Digital MUX Breakout
  S1 = NKK M2032SS1W01 3PDT Toggle Switch [part_number=M2032SS1W03 package=THT]  # not connected
  S2 = NKK M2032SS1W01 3PDT Toggle Switch [part_number=M2032SS1W03 package=THT]  # not connected
  S3 = NKK M2032SS1W01 3PDT Toggle Switch [part_number=M2032SS1W03 package=THT]  # not connected
  S4 = NKK M2032SS1W01 3PDT Toggle Switch [part_number=M2032SS1W03 package=THT]  # not connected
  S5 = Momentary Switch [package=ksa_sealed_tac_switch]  # not connected
  S6 = Momentary Switch [package=ksa_sealed_tac_switch]  # not connected
  S7 = Momentary Switch [package=ksa_sealed_tac_switch]  # not connected
  S8 = Momentary Switch [package=ksa_sealed_tac_switch]  # not connected
  S9 = NKK M2032SS1W01 3PDT Toggle Switch [part_number=M2032SS1W03 package=THT]  # not connected
  switch1 = Rotary_Switch_12x1  # not connected
  switch2 = Rotary_Switch_12x1  # not connected
  switch3 = Rotary_Switch_12x1  # not connected
  S10 = Momentary Switch [package=ksa_sealed_tac_switch]  # not connected
  S11 = Momentary Switch [package=ksa_sealed_tac_switch]  # not connected
  S12 = Momentary Switch [package=ksa_sealed_tac_switch]  # not connected
  LED1 = smd LED [color="Orange (620nm)" package="0805 [SMD]"]  # not connected
  LED2 = smd LED [color="Orange (620nm)" package="0805 [SMD]"]  # not connected
  LED3 = smd LED [color="Orange (620nm)" package="0805 [SMD]"]  # not connected
  LED4 = smd LED [color="Orange (620nm)" package="0805 [SMD]"]  # not connected
  LED5 = smd LED [color="Orange (620nm)" package="0805 [SMD]"]  # not connected
  LED6 = smd LED [color="Orange (620nm)" package="0805 [SMD]"]  # not connected
  LED7 = smd LED [color="Orange (620nm)" package="0805 [SMD]"]  # not connected
  LED8 = smd LED [color="Orange (620nm)" package="0805 [SMD]"]  # not connected
  LED9 = smd LED [color="Orange (620nm)" package="0805 [SMD]"]  # not connected
  LED10 = smd LED [color="Orange (620nm)" package="0805 [SMD]"]  # not connected
  LED11 = smd LED [color="Orange (620nm)" package="0805 [SMD]"]  # not connected
  LED12 = smd LED [color="Orange (620nm)" package="0805 [SMD]"]  # not connected
  LED13 = smd LED [color="Orange (620nm)" package="0805 [SMD]"]  # not connected
  LED14 = smd LED [color="Orange (620nm)" package="0805 [SMD]"]  # not connected
  LED15 = smd LED [color="Orange (620nm)" package="0805 [SMD]"]  # not connected
  LED16 = smd LED [color="Orange (620nm)" package="0805 [SMD]"]  # not connected
  LED17 = smd LED [color="Green (570nm)" package="0805 [SMD]"]  # not connected
  LED18 = smd LED [color="Green (570nm)" package="0805 [SMD]"]  # not connected
  LED19 = smd LED [color="Green (570nm)" package="0805 [SMD]"]  # not connected
  LED20 = smd LED [color="Green (570nm)" package="0805 [SMD]"]  # not connected
  LED21 = smd LED [color="Green (570nm)" package="0805 [SMD]"]  # not connected
  LED22 = smd LED [color="Green (570nm)" package="0805 [SMD]"]  # not connected
  LED23 = smd LED [color="Green (570nm)" package="0805 [SMD]"]  # not connected
  LED24 = smd LED [color="Green (570nm)" package="0805 [SMD]"]  # not connected
  LED25 = smd LED [color="Red (660nm)" package="0805 [SMD]"]  # not connected
  LED26 = smd LED [color="Red (660nm)" package="0805 [SMD]"]  # not connected
  LED27 = smd LED [color="White (4500K)" package="0805 [SMD]"]  # not connected
  LED28 = smd LED [color="White (4500K)" package="0805 [SMD]"]  # not connected
  LED29 = smd LED [color="Orange (620nm)" package="0805 [SMD]"]  # not connected
  LED30 = smd LED [color="Orange (620nm)" package="0805 [SMD]"]  # not connected
  S13 = NKK M2032SS1W01 3PDT Toggle Switch [part_number=M2032SS1W03 package=THT]  # not connected
  DM13A_2 = MAX7219 [package=dil24]
  Mux_2 = Analog Digital MUX Breakout
  J1 = Camdenboss CTB0158-6 [part_number=CTB0158-6 package=THT]  # not connected
  Common_GND = Camdenboss CTB0158-4 [part_number=CTB0158-4 package=THT]
  R2 = Resistor [tolerance=±5% resistance=1.8k package="2512 [SMD]"]
  R1 = Resistor [tolerance=±5% resistance=1.8k package="2512 [SMD]"]
  Common_GND1 = Camdenboss CTB0158-4 [part_number=CTB0158-4 package=THT]
  R3 = Resistor [tolerance=±5% power=0.25 resistance=1.8k package=THT]
  R4 = Resistor [tolerance=±5% power=0.25 resistance=1.2k package=THT]
  R5 = Resistor [tolerance=±5% power=0.25 resistance=1.2k package=THT]
  LED_VCC_+5V = Battery
  Common_VCC_LED = Camdenboss CTB0158-4 [part_number=CTB0158-4 package=THT]

nets:
  N1: DM13A.DIN, DM13A_2.DIN
  N2: DM13A.DIG4, DM13A_2.DIG4
  GND: DM13A.GND, DM13A_2.GND
  N3: DM13A.SEGE, DM13A_2.SEGE, Common_GND1.terminal_1, R3.Pin_1, R4.Pin_1, R5.Pin_1
  N4: DM13A.SEGDP, DM13A_2.DIG0
  N5: DM13A.SEGD, R4.Pin_0
  VCC: DM13A.DOUT, RSC_Master_Board1.5V, Mux.VCC, DM13A_2.DOUT, Mux_2.VCC, R2.Pin_1, R1.Pin_1
  N6: RSC_Master_Board1.GND, Common_GND.pin2
  GND_2: Mux.GND, Mux.EN, Mux_2.GND, Mux_2.EN, Common_GND.pin1
  N7: Mux.S0, Mux_2.S0
  N8: Mux.S1, Mux_2.S1
  N9: Mux.S2, Mux_2.S2
  N10: Mux.S3, Mux_2.S3
  N11: Mux.SIG, R1.Pin_0
  N12: DM13A_2.SEGD, R5.Pin_0
  N13: Mux_2.SIG, R2.Pin_0
  N14: Common_GND1.terminal_4, LED_VCC_+5V.-
  N15: LED_VCC_+5V.+, Common_VCC_LED.terminal_3

notes:
  Mach_Warn_Test(2)
  Speed_Warn_Test(1)
  Stall_Warn_Test_R(2)
  Stall_Warn_Test(1)
  signal - pin 30 arduino
  signal - pin 31 arduino
  Flight_Rec_Test
  Oxy_pass_sw
  pin 22 arduino
  pin 23 arduino
  pin 24 arduino
  pin 25 arduino
  VCC - Arduino
  EEC_Eng_R
  EEC_Eng_L
  ELT_ARM
  IRS_Data_Sel
  IRS_Sys_Sel
  IRS_L_Mode
  IRS_R_Mode
  22 - S0
  23 - S1
  24 - S2
  25 - S3
  26 - S
  29 - T
  27 - L
  28 - D
  D - pin 28 arduino
  Signal - pin 32 arduino
  L - pin 27 arduino
  Ext_Comm_Jack

custom parts:
  NKK M2032SS1W01 3PDT Toggle Switch: NKK M2032SS1W01 3PDT Toggle Switch This switch has three poles and two position (Jan 2022 replace pads in pcb with pads with holes)
