# Fritzing sketch B737_Overhead_Panel_with_LEDs (saved by Fritzing 0.9.10b)

parts:
  RSC_Master_Board = Arduino Mega 2560 (Rev3)  # not connected
  7_Segment1 = 7 Segment Display  # not connected
  7_Segment2 = 7 Segment Display  # not connected
  7_Segment3 = 7 Segment Display  # not connected
  7_Segment4 = 7 Segment Display  # not connected
  7_Segment5 = 7 Segment Display  # not connected
  LED1 = LED - 5mm [color="Orange (620nm)" current=0.030 package="5 mm [THT]"]
  LED2 = LED - 5mm [color="Orange (620nm)" current=0.030 package="5 mm [THT]"]
  LED3 = LED - 5mm [color="Orange (620nm)" current=0.030 package="5 mm [THT]"]
  LED6 = LED - 5mm [color="Orange (620nm)" current=0.030 package="5 mm [THT]"]
  LED7 = LED - 5mm [color="Orange (620nm)" current=0.030 package="5 mm [THT]"]
  LED8 = LED - 5mm [color="Orange (620nm)" current=0.030 package="5 mm [THT]"]
  LED9 = LED - 5mm [color="Orange (620nm)" current=0.030 package="5 mm [THT]"]
  LED10 = LED - 5mm [color="Orange (620nm)" current=0.030 package="5 mm [THT]"]
  LED11 = LED - 5mm [color="White (6500K)" current=0.030 package="5 mm [THT]"]
  LED12 = LED - 5mm [color="White (6500K)" current=0.030 package="5 mm [THT]"]
  LED13 = LED - 5mm [color="White (6500K)" current=0.030 package="5 mm [THT]"]
  LED14 = LED - 5mm [color="White (6500K)" current=0.030 package="5 mm [THT]"]
  LED15 = LED - 5mm [color="White (6500K)" current=0.030 package="5 mm [THT]"]
  LED16 = LED - 5mm [color="Orange (620nm)" current=0.030 package="5 mm [THT]"]
  LED17 = LED - 5mm [color="Orange (620nm)" current=0.030 package="5 mm [THT]"]
  LED18 = LED - 5mm [color="Orange (620nm)" current=0.030 package="5 mm [THT]"]
  LED19 = LED - 5mm [color="Orange (620nm)" current=0.030 package="5 mm [THT]"]
  LED20 = LED - 5mm [color="Orange (620nm)" current=0.030 package="5 mm [THT]"]
  LED21 = LED - 5mm [color="Orange (620nm)" current=0.030 package="5 mm [THT]"]
  LED22 = LED - 5mm [color="Orange (620nm)" current=0.030 package="5 mm [THT]"]
  LED23 = LED - 5mm [color="Orange (620nm)" current=0.030 package="5 mm [THT]"]
  LED24 = LED - 5mm [color="White (6500K)" current=0.030 package="5 mm [THT]"]  # not connected
  LED25 = LED - 5mm [color="Orange (620nm)" current=0.030 package="5 mm [THT]"]  # not connected
  LED26 = LED - 5mm [color="Orange (620nm)" current=0.030 package="5 mm [THT]"]  # not connected
  LED27 = LED - 5mm [color="Orange (620nm)" current=0.030 package="5 mm [THT]"]  # not connected
  LED28 = LED - 5mm [color="Orange (620nm)" current=0.030 package="5 mm [THT]"]
  LED29 = LED - 5mm [color="Orange (620nm)" current=0.030 package="5 mm [THT]"]
  LED30 = LED - 5mm [color="Orange (620nm)" current=0.030 package="5 mm [THT]"]  # not connected
  LED31 = LED - 5mm [color="Orange (620nm)" current=0.030 package="5 mm [THT]"]
  LED32 = LED - 5mm [color="White (6500K)" current=0.030 package="5 mm [THT]"]
  LED33 = LED - 5mm [color="White (6500K)" current=0.030 package="5 mm [THT]"]
  LED34 = LED - 5mm [color="White (6500K)" current=0.030 package="5 mm [THT]"]  # not connected
  LED35 = LED - 5mm [color="White (6500K)" current=0.030 package="5 mm [THT]"]
  LED36 = LED - 5mm [color="Orange (620nm)" current=0.030 package="5 mm [THT]"]
  LED37 = LED - 5mm [color="Orange (620nm)" current=0.030 package="5 mm [THT]"]
  LED38 = LED - 5mm [color="Orange (620nm)" current=0.030 package="5 mm [THT]"]
  LED39 = LED - 5mm [color="White (6500K)" current=0.030 package="5 mm [THT]"]  # not connected
  LED40 = LED - 5mm [color="Orange (620nm)" current=0.030 package="5 mm [THT]"]  # not connected
  LED41 = LED - 5mm [color="Orange (620nm)" current=0.030 package="5 mm [THT]"]  # not connected
  LED42 = LED - 5mm [color="Orange (620nm)" current=0.030 package="5 mm [THT]"]  # not connected
  LED43 = LED - 5mm [color="White (6500K)" current=0.030 package="5 mm [THT]"]  # not connected
  LED44 = LED - 5mm [color="Orange (620nm)" current=0.030 package="5 mm [THT]"]  # not connected
  LED45 = LED - 5mm [color="Orange (620nm)" current=0.030 package="5 mm [THT]"]  # not connected
  LED46 = LED - 5mm [color="Orange (620nm)" current=0.030 package="5 mm [THT]"]  # not connected
  LED47 = LED - 5mm [color="Orange (620nm)" current=0.030 package="5 mm [THT]"]  # not connected
  LED48 = LED - 5mm [color="Orange (620nm)" current=0.030 package="5 mm [THT]"]  # not connected
  LED49 = LED - 5mm [color="Orange (620nm)" current=0.030 package="5 mm [THT]"]  # not connected
  LED50 = LED - 5mm [color="Orange (620nm)" current=0.030 package="5 mm [THT]"]  # not connected
  LED51 = LED - 5mm [color="Orange (620nm)" current=0.030 package="5 mm [THT]"]  # not connected
  LED52 = LED - 5mm [color="Green (570nm)" current=0.030 package="5 mm [THT]"]  # not connected
  LED53 = LED - 5mm [color="Green (570nm)" current=0.030 package="5 mm [THT]"]  # not connected
  LED54 = LED - 5mm [color="Green (570nm)" current=0.030 package="5 mm [THT]"]  # not connected
  LED55 = LED - 5mm [color="Green (570nm)" current=0.030 package="5 mm [THT]"]  # not connected
  LED56 = LED - 5mm [color="Orange (620nm)" current=0.030 package="5 mm [THT]"]  # not connected
  LED57 = LED - 5mm [color="Orange (620nm)" current=0.030 package="5 mm [THT]"]  # not connected
  LED58 = LED - 5mm [color="Orange (620nm)" current=0.030 package="5 mm [THT]"]  # not connected
  LED59 = LED - 5mm [color="Orange (620nm)" current=0.030 package="5 mm [THT]"]  # not connected
  LED60 = LED - 5mm [color="Orange (620nm)" current=0.030 package="5 mm [THT]"]  # not connected
  LED61 = LED - 5mm [color="Orange (620nm)" current=0.030 package="5 mm [THT]"]  # not connected
  LED62 = LED - 5mm [color="Orange (620nm)" current=0.030 package="5 mm [THT]"]  # not connected
  LED63 = LED - 5mm [color="Orange (620nm)" current=0.030 package="5 mm [THT]"]  # not connected
  S60 = Momentary Switch [package=ksa_sealed_tac_switch]  # not connected
  LED64 = LED - 5mm [color="Orange (620nm)" current=0.030 package="5 mm [THT]"]  # not connected
  LED65 = LED - 5mm [color="Orange (620nm)" current=0.030 package="5 mm [THT]"]  # not connected
  LED66 = LED - 5mm [color="Orange (620nm)" current=0.030 package="5 mm [THT]"]  # not connected
  LED67 = LED - 5mm [color="White (6500K)" current=0.030 package="5 mm [THT]"]  # not connected
  LED68 = LED - 5mm [color="White (6500K)" current=0.030 package="5 mm [THT]"]  # not connected
  LED69 = LED - 5mm [color="White (6500K)" current=0.030 package="5 mm [THT]"]  # not connected
  LED70 = LED - 5mm [color="White (6500K)" current=0.030 package="5 mm [THT]"]  # not connected
  LED71 = LED - 5mm [color="White (6500K)" current=0.030 package="5 mm [THT]"]
  LED72 = LED - 5mm [color="White (6500K)" current=0.030 package="5 mm [THT]"]
  LED73 = LED - 5mm [color="Orange (620nm)" current=0.030 package="5 mm [THT]"]
  LED74 = LED - 5mm [color="Orange (620nm)" current=0.030 package="5 mm [THT]"]  # not connected
  LED75 = LED - 5mm [color="Orange (620nm)" current=0.030 package="5 mm [THT]"]  # not connected
  LED76 = LED - 5mm [color="Orange (620nm)" current=0.030 package="5 mm [THT]"]  # not connected
  LED77 = LED - 5mm [color="Orange (620nm)" current=0.030 package="5 mm [THT]"]  # not connected
  LED78 = LED - 5mm [color="Orange (620nm)" current=0.030 package="5 mm [THT]"]  # not connected
  LED79 = LED - 5mm [color="Orange (620nm)" current=0.030 package="5 mm [THT]"]  # not connected
  LED80 = LED - 5mm [color="Orange (620nm)" current=0.030 package="5 mm [THT]"]  # not connected
  LED81 = LED - 5mm [color="Orange (620nm)" current=0.030 package="5 mm [THT]"]  # not connected
  LED83 = LED - 5mm [color="Orange (620nm)" current=0.030 package="5 mm [THT]"]  # not connected
  LED84 = LED - 5mm [color="Orange (620nm)" current=0.030 package="5 mm [THT]"]  # not connected
  LED85 = LED - 5mm [color="Orange (620nm)" current=0.030 package="5 mm [THT]"]  # not connected
  LED86 = LED - 5mm [color="Orange (620nm)" current=0.030 package="5 mm [THT]"]  # not connected
  LED87 = LED - 5mm [color="Orange (620nm)" current=0.030 package="5 mm [THT]"]  # not connected
  LED89 = LED - 5mm [color="Orange (620nm)" current=0.030 package="5 mm [THT]"]  # not connected
  LED90 = LED - 5mm [color="Orange (620nm)" current=0.030 package="5 mm [THT]"]  # not connected
  LED91 = LED - 5mm [color="Orange (620nm)" current=0.030 package="5 mm [THT]"]  # not connected
  LED92 = LED - 5mm [color="Orange (620nm)" current=0.030 package="5 mm [THT]"]  # not connected
  LED93 = LED - 5mm [color="Orange (620nm)" current=0.030 package="5 mm [THT]"]  # not connected
  LED94 = LED - 5mm [color="Orange (620nm)" current=0.030 package="5 mm [THT]"]
  LED95 = LED - 5mm [color="Orange (620nm)" current=0.030 package="5 mm [THT]"]
  LED96 = LED - 5mm [color="Orange (620nm)" current=0.030 package="5 mm [THT]"]
  LED97 = LED - 5mm [color="Orange (620nm)" current=0.030 package="5 mm [THT]"]
  LED98 = LED - 5mm [color="Orange (620nm)" current=0.030 package="5 mm [THT]"]
  LED99 = LED - 5mm [color="Orange (620nm)" current=0.030 package="5 mm [THT]"]
  LED100 = LED - 5mm [color="Orange (620nm)" current=0.030 package="5 mm [THT]"]
  LED101 = LED - 5mm [color="Orange (620nm)" current=0.030 package="5 mm [THT]"]
  LED102 = LED - 5mm [color="Orange (620nm)" current=0.030 package="5 mm [THT]"]
  LED103 = LED - 5mm [color="Orange (620nm)" current=0.030 package="5 mm [THT]"]
  LED104 = LED - 5mm [color="Orange (620nm)" current=0.030 package="5 mm [THT]"]
  LED105 = LED - 5mm [color="Green (570nm)" current=0.030 package="5 mm [THT]"]
  LED106 = LED - 5mm [color="Green (570nm)" current=0.030 package="5 mm [THT]"]
  DM13A = MAX7219 [package=dil24]
  GND = STARBOARD_GND [package=starboard_ground_small]  # not connected
  LED107 = LED - 5mm [color="Orange (620nm)" current=0.030 package="5 mm [THT]"]
  LED108 = LED - 5mm [color="Orange (620nm)" current=0.030 package="5 mm [THT]"]
  GND1 = STARBOARD_GND [package=starboard_ground_small]  # not connected
  DM13A1 = MAX7219 [package=dil24]
  DM13A2 = MAX7219 [package=dil24]  # not connected
  DM13A3 = MAX7219 [package=dil24]

nets:
  N1: LED1.anode, DM13A.CLK
  N2: LED2.anode, DM13A.SEGA
  N3: LED3.anode, DM13A.SEGF
  N4: LED6.anode, DM13A.VCC
  N5: LED7.anode, DM13A.SEGC
  N6: LED8.anode, DM13A.LOAD
  N7: LED9.anode, DM13A.DIG1
  N8: LED10.anode, DM13A.ISET
  N9: LED11.anode, DM13A.DIG5
  N10: LED12.anode, DM13A.DIG7
  N11: LED13.anode, DM13A.GND2
  N12: LED14.anode, DM13A.DIG3
  N13: LED15.anode, DM13A.DIG6
  N14: LED16.anode, DM13A.DIG2
  N15: LED17.anode, DM13A1.CLK
  N16: LED18.anode, DM13A1.SEGA
  N17: LED19.anode, DM13A1.SEGF
  N18: LED20.anode, DM13A1.SEGB
  N19: LED21.anode, DM13A1.VCC
  N20: LED22.anode, DM13A1.SEGG
  N21: LED23.anode, DM13A1.ISET
  N22: LED28.anode, DM13A1.SEGC
  N23: LED29.anode, DM13A1.DIG3
  N24: LED31.anode, DM13A1.DIG6
  N25: LED32.anode, DM13A1.LOAD
  N26: LED33.anode, DM13A1.DIG7
  N27: LED35.anode, DM13A1.DIG1
  N28: LED36.anode, DM13A1.DIG5
  N29: LED37.anode, DM13A1.GND2
  N30: LED38.anode, DM13A1.DIG2
  N31: LED71.anode, DM13A3.GND2
  N32: LED72.anode, DM13A3.DIG5
  N33: LED73.anode, DM13A3.DIG7
  N34: LED94.anode, DM13A3.DIG6
  N35: LED95.anode, DM13A3.DIG2
  N36: LED96.anode, DM13A3.DIG3
  N37: LED97.anode, DM13A3.DIG1
  N38: LED98.anode, DM13A3.VCC
  N39: LED99.anode, DM13A3.SEGC
  N40: LED100.anode, DM13A3.SEGG
  N41: LED101.anode, DM13A3.LOAD
  N42: LED102.anode, DM13A3.ISET
  N43: LED103.anode, DM13A3.SEGB
  N44: LED104.anode, DM13A3.SEGF
  N45: LED105.anode, DM13A3.SEGA
  N46: LED106.anode, DM13A3.CLK
  N47: DM13A.SEGB, LED108.anode
  N48: DM13A.SEGG, LED107.anode
