# Fritzing sketch B737_Overhead_Panel_with_switches_and_LEDs (saved by Fritzing 0.9.10b)

parts:
  RSC_Master_Board = Arduino Mega 2560 (Rev3)
  Mux1 = Analog Digital MUX Breakout
  Mux2 = Analog Digital MUX Breakout  # not connected
  Mux3 = Analog Digital MUX Breakout
  Mux4 = Analog Digital MUX Breakout
  R1 = Resistor [tolerance=±5% power=0.25 resistance=5k package=THT]
  S1 = Taiway 100-SP-X-T1 SPDT Miniature Toggle Switch [part_number=100-SP-X-T1-0-0-B1-M2 package=THT]
  S2 = Taiway 100-SP-X-T1 SPDT Miniature Toggle Switch [part_number=100-SP-X-T1-0-0-B1-M2 package=THT]
  S3 = Taiway 100-SP-X-T1 SPDT Miniature Toggle Switch [part_number=100-SP-X-T1-0-0-B1-M2 package=THT]
  S4 = Taiway 100-SP-X-T1 SPDT Miniature Toggle Switch [part_number=100-SP-X-T1-0-0-B1-M2 package=THT]
  S5 = Taiway 100-SP-X-T1 SPDT Miniature Toggle Switch [part_number=100-SP-X-T1-0-0-B1-M2 package=THT]
  S6 = Taiway 100-SP-X-T1 SPDT Miniature Toggle Switch [part_number=100-SP-X-T1-0-0-B1-M2 package=THT]
  S7 = Taiway 100-SP-X-T1 SPDT Miniature Toggle Switch [part_number=100-SP-X-T1-0-0-B1-M2 package=THT]
  S8 = Taiway 100-SP-X-T1 SPDT Miniature Toggle Switch [part_number=100-SP-X-T1-0-0-B1-M2 package=THT]
  S9 = Taiway 100-SP-X-T1 SPDT Miniature Toggle Switch [part_number=100-SP-X-T1-0-0-B1-M2 package=THT]
  S10 = Taiway 100-SP-X-T1 SPDT Miniature Toggle Switch [part_number=100-SP-X-T1-0-0-B1-M2 package=THT]  # not connected
  S11 = Taiway 100-SP-X-T1 SPDT Miniature Toggle Switch [part_number=100-SP-X-T1-0-0-B1-M2 package=THT]  # not connected
  S12 = Taiway 100-SP-X-T1 SPDT Miniature Toggle Switch [part_number=100-SP-X-T1-0-0-B1-M2 package=THT]  # not connected
  S13 = Taiway 100-SP-X-T1 SPDT Miniature Toggle Switch [part_number=100-SP-X-T1-0-0-B1-M2 package=THT]  # not connected
  S14 = Taiway 100-SP-X-T1 SPDT Miniature Toggle Switch [part_number=100-SP-X-T1-0-0-B1-M2 package=THT]  # not connected
  S15 = Taiway 100-SP-X-T1 SPDT Miniature Toggle Switch [part_number=100-SP-X-T1-0-0-B1-M2 package=THT]  # not connected
  S16 = Taiway 100-SP-X-T1 SPDT Miniature Toggle Switch [part_number=100-SP-X-T1-0-0-B1-M2 package=THT]  # not connected
  S17 = Taiway 100-SP-X-T1 SPDT Miniature Toggle Switch [part_number=100-SP-X-T1-0-0-B1-M2 package=THT]  # not connected
  S18 = Taiway 100-SP-X-T1 SPDT Miniature Toggle Switch [part_number=100-SP-X-T1-0-0-B1-M2 package=THT]  # not connected
  S19 = Taiway 100-SP-X-T1 SPDT Miniature Toggle Switch [part_number=100-SP-X-T1-0-0-B1-M2 package=THT]  # not connected
  S20 = Taiway 100-SP-X-T1 SPDT Miniature Toggle Switch [part_number=100-SP-X-T1-0-0-B1-M2 package=THT]  # not connected
  S21 = Taiway 100-SP-X-T1 SPDT Miniature Toggle Switch [part_number=100-SP-X-T1-0-0-B1-M2 package=THT]  # not connected
  S22 = Taiway 100-SP-X-T1 SPDT Miniature Toggle Switch [part_number=100-SP-X-T1-0-0-B1-M2 package=THT]  # not connected
  S23 = Taiway 100-SP-X-T1 SPDT Miniature Toggle Switch [part_number=100-SP-X-T1-0-0-B1-M2 package=THT]  # not connected
  L1 = Solenoid  # not connected
  S24 = Taiway 100-SP-X-T1 SPDT Miniature Toggle Switch [part_number=100-SP-X-T1-0-0-B1-M2 package=THT]
  7_Segment1 = 7 Segment Display  # not connected
  7_Segment2 = 7 Segment Display  # not connected
  7_Segment3 = 7 Segment Display  # not connected
  7_Segment4 = 7 Segment Display  # not connected
  7_Segment5 = 7 Segment Display  # not connected
  LED1 = LED - 5mm [color="Orange (620nm)" current=0.030 package="5 mm [THT]"]
  LED2 = LED - 5mm [color="Orange (620nm)" current=0.030 package="5 mm [THT]"]
  LED3 = LED - 5mm [color="Orange (620nm)" current=0.030 package="5 mm [THT]"]
  LED6 = LED - 5mm [color="Orange (620nm)" current=0.030 package="5 mm [THT]"]
  LED7 = LED - 5mm [color="Orange (620nm)" current=0.030 package="5 mm [THT]"]
  LED8 = LED - 5mm [color="Orange (620nm)" current=0.030 package="5 mm [THT]"]
  LED9 = LED - 5mm [color="Orange (620nm)" current=0.030 package="5 mm [THT]"]
  LED10 = LED - 5mm [color="Orange (620nm)" current=0.030 package="5 mm [THT]"]
  LED11 = LED - 5mm [color="White (6500K)" current=0.030 package="5 mm [THT]"]  # not connected
  LED12 = LED - 5mm [color="White (6500K)" current=0.030 package="5 mm [THT]"]  # not connected
  LED13 = LED - 5mm [color="White (6500K)" current=0.030 package="5 mm [THT]"]  # not connected
  LED14 = LED - 5mm [color="White (6500K)" current=0.030 package="5 mm [THT]"]  # not connected
  LED15 = LED - 5mm [color="White (6500K)" current=0.030 package="5 mm [THT]"]  # not connected
  LED16 = LED - 5mm [color="Orange (620nm)" current=0.030 package="5 mm [THT]"]  # not connected
  LED17 = LED - 5mm [color="Orange (620nm)" current=0.030 package="5 mm [THT]"]  # not connected
  LED18 = LED - 5mm [color="Orange (620nm)" current=0.030 package="5 mm [THT]"]  # not connected
  LED19 = LED - 5mm [color="Orange (620nm)" current=0.030 package="5 mm [THT]"]  # not connected
  LED20 = LED - 5mm [color="Orange (620nm)" current=0.030 package="5 mm [THT]"]  # not connected
  LED21 = LED - 5mm [color="Orange (620nm)" current=0.030 package="5 mm [THT]"]  # not connected
  LED22 = LED - 5mm [color="Orange (620nm)" current=0.030 package="5 mm [THT]"]  # not connected
  LED23 = LED - 5mm [color="Orange (620nm)" current=0.030 package="5 mm [THT]"]  # not connected
  S25 = Momentary Switch [package=ksa_sealed_tac_switch]  # not connected
  LED24 = LED - 5mm [color="White (6500K)" current=0.030 package="5 mm [THT]"]  # not connected
  LED25 = LED - 5mm [color="Orange (620nm)" current=0.030 package="5 mm [THT]"]  # not connected
  LED26 = LED - 5mm [color="Orange (620nm)" current=0.030 package="5 mm [THT]"]  # not connected
  LED27 = LED - 5mm [color="Orange (620nm)" current=0.030 package="5 mm [THT]"]  # not connected
  S26 = Taiway 100-SP-X-T1 SPDT Miniature Toggle Switch [part_number=100-SP-X-T1-0-0-B1-M2 package=THT]  # not connected
  S27 = Momentary Switch [package=ksa_sealed_tac_switch]  # not connected
  S28 = Momentary Switch [package=ksa_sealed_tac_switch]  # not connected
  LED28 = LED - 5mm [color="Orange (620nm)" current=0.030 package="5 mm [THT]"]  # not connected
  LED29 = LED - 5mm [color="Orange (620nm)" current=0.030 package="5 mm [THT]"]  # not connected
  LED30 = LED - 5mm [color="Orange (620nm)" current=0.030 package="5 mm [THT]"]  # not connected
  LED31 = LED - 5mm [color="Orange (620nm)" current=0.030 package="5 mm [THT]"]  # not connected
  LED32 = LED - 5mm [color="White (6500K)" current=0.030 package="5 mm [THT]"]  # not connected
  LED33 = LED - 5mm [color="White (6500K)" current=0.030 package="5 mm [THT]"]  # not connected
  LED34 = LED - 5mm [color="White (6500K)" current=0.030 package="5 mm [THT]"]  # not connected
  S29 = Taiway 100-SP-X-T1 SPDT Miniature Toggle Switch [part_number=100-SP-X-T1-0-0-B1-M2 package=THT]  # not connected
  S30 = Momentary Switch [package=ksa_sealed_tac_switch]  # not connected
  S32 = Momentary Switch [package=ksa_sealed_tac_switch]  # not connected
  S33 = Momentary Switch [package=ksa_sealed_tac_switch]  # not connected
  switch1 = Rotary_Switch_12x1  # not connected
  LED35 = LED - 5mm [color="White (6500K)" current=0.030 package="5 mm [THT]"]  # not connected
  LED36 = LED - 5mm [color="Orange (620nm)" current=0.030 package="5 mm [THT]"]  # not connected
  LED37 = LED - 5mm [color="Orange (620nm)" current=0.030 package="5 mm [THT]"]  # not connected
  LED38 = LED - 5mm [color="Orange (620nm)" current=0.030 package="5 mm [THT]"]  # not connected
  S34 = Taiway 100-SP-X-T1 SPDT Miniature Toggle Switch [part_number=100-SP-X-T1-0-0-B1-M2 package=THT]  # not connected
  switch2 = Rotary_Switch_12x1  # not connected
  switch3 = Rotary_Switch_12x1  # not connected
  switch4 = Rotary_Switch_12x1  # not connected
  S35 = Taiway 100-SP-X-T1 SPDT Miniature Toggle Switch [part_number=100-SP-X-T1-0-0-B1-M2 package=THT]  # not connected
  S36 = Taiway 100-SP-X-T1 SPDT Miniature Toggle Switch [part_number=100-SP-X-T1-0-0-B1-M2 package=THT]  # not connected
  S37 = Taiway 100-SP-X-T1 SPDT Miniature Toggle Switch [part_number=100-SP-X-T1-0-0-B1-M2 package=THT]  # not connected
  S38 = Taiway 100-SP-X-T1 SPDT Miniature Toggle Switch [part_number=100-SP-X-T1-0-0-B1-M2 package=THT]  # not connected
  S39 = Taiway 100-SP-X-T1 SPDT Miniature Toggle Switch [part_number=100-SP-X-T1-0-0-B1-M2 package=THT]  # not connected
  S40 = Taiway 100-SP-X-T1 SPDT Miniature Toggle Switch [part_number=100-SP-X-T1-0-0-B1-M2 package=THT]  # not connected
  S41 = Momentary Switch [package=ksa_sealed_tac_switch]  # not connected
  S42 = Taiway 100-SP-X-T1 SPDT Miniature Toggle Switch [part_number=100-SP-X-T1-0-0-B1-M2 package=THT]  # not connected
  S43 = Momentary Switch [package=ksa_sealed_tac_switch]  # not connected
  S44 = Momentary Switch [package=ksa_sealed_tac_switch]  # not connected
  LED39 = LED - 5mm [color="White (6500K)" current=0.030 package="5 mm [THT]"]  # not connected
  LED40 = LED - 5mm [color="Orange (620nm)" current=0.030 package="5 mm [THT]"]  # not connected
  LED41 = LED - 5mm [color="Orange (620nm)" current=0.030 package="5 mm [THT]"]  # not connected
  LED42 = LED - 5mm [color="Orange (620nm)" current=0.030 package="5 mm [THT]"]  # not connected
  S45 = Taiway 100-SP-X-T1 SPDT Miniature Toggle Switch [part_number=100-SP-X-T1-0-0-B1-M2 package=THT]  # not connected
  S46 = Taiway 100-SP-X-T1 SPDT Miniature Toggle Switch [part_number=100-SP-X-T1-0-0-B1-M2 package=THT]  # not connected
  S47 = Taiway 100-SP-X-T1 SPDT Miniature Toggle Switch [part_number=100-SP-X-T1-0-0-B1-M2 package=THT]  # not connected
  switch5 = Rotary_Switch_12x1  # not connected
  switch6 = Rotary_Switch_12x1  # not connected
  LED43 = LED - 5mm [color="White (6500K)" current=0.030 package="5 mm [THT]"]  # not connected
  switch7 = Rotary_Switch_12x1  # not connected
  switch8 = Rotary_Switch_12x1  # not connected
  LED44 = LED - 5mm [color="Orange (620nm)" current=0.030 package="5 mm [THT]"]  # not connected
  S48 = Taiway 100-SP-X-T1 SPDT Miniature Toggle Switch [part_number=100-SP-X-T1-0-0-B1-M2 package=THT]  # not connected
  S49 = Taiway 100-SP-X-T1 SPDT Miniature Toggle Switch [part_number=100-SP-X-T1-0-0-B1-M2 package=THT]  # not connected
  LED45 = LED - 5mm [color="Orange (620nm)" current=0.030 package="5 mm [THT]"]  # not connected
  LED46 = LED - 5mm [color="Orange (620nm)" current=0.030 package="5 mm [THT]"]  # not connected
  LED47 = LED - 5mm [color="Orange (620nm)" current=0.030 package="5 mm [THT]"]  # not connected
  S50 = Taiway 100-SP-X-T1 SPDT Miniature Toggle Switch [part_number=100-SP-X-T1-0-0-B1-M2 package=THT]  # not connected
  S51 = Taiway 100-SP-X-T1 SPDT Miniature Toggle Switch [part_number=100-SP-X-T1-0-0-B1-M2 package=THT]  # not connected
  S52 = Taiway 100-SP-X-T1 SPDT Miniature Toggle Switch [part_number=100-SP-X-T1-0-0-B1-M2 package=THT]  # not connected
  LED48 = LED - 5mm [color="Orange (620nm)" current=0.030 package="5 mm [THT]"]  # not connected
  LED49 = LED - 5mm [color="Orange (620nm)" current=0.030 package="5 mm [THT]"]  # not connected
  LED50 = LED - 5mm [color="Orange (620nm)" current=0.030 package="5 mm [THT]"]  # not connected
  LED51 = LED - 5mm [color="Orange (620nm)" current=0.030 package="5 mm [THT]"]  # not connected
  LED52 = LED - 5mm [color="Green (570nm)" current=0.030 package="5 mm [THT]"]  # not connected
  LED53 = LED - 5mm [color="Green (570nm)" current=0.030 package="5 mm [THT]"]  # not connected
  LED54 = LED - 5mm [color="Green (570nm)" current=0.030 package="5 mm [THT]"]  # not connected
  LED55 = LED - 5mm [color="Green (570nm)" current=0.030 package="5 mm [THT]"]  # not connected
  LED56 = LED - 5mm [color="Orange (620nm)" current=0.030 package="5 mm [THT]"]  # not connected
  LED57 = LED - 5mm [color="Orange (620nm)" current=0.030 package="5 mm [THT]"]  # not connected
  LED58 = LED - 5mm [color="Orange (620nm)" current=0.030 package="5 mm [THT]"]  # not connected
  LED59 = LED - 5mm [color="Orange (620nm)" current=0.030 package="5 mm [THT]"]  # not connected
  LED60 = LED - 5mm [color="Orange (620nm)" current=0.030 package="5 mm [THT]"]  # not connected
  LED61 = LED - 5mm [color="Orange (620nm)" current=0.030 package="5 mm [THT]"]  # not connected
  LED62 = LED - 5mm [color="Orange (620nm)" current=0.030 package="5 mm [THT]"]  # not connected
  LED63 = LED - 5mm [color="Orange (620nm)" current=0.030 package="5 mm [THT]"]  # not connected
  S53 = Taiway 100-SP-X-T1 SPDT Miniature Toggle Switch [part_number=100-SP-X-T1-0-0-B1-M2 package=THT]  # not connected
  S54 = Taiway 100-SP-X-T1 SPDT Miniature Toggle Switch [part_number=100-SP-X-T1-0-0-B1-M2 package=THT]  # not connected
  S55 = Taiway 100-SP-X-T1 SPDT Miniature Toggle Switch [part_number=100-SP-X-T1-0-0-B1-M2 package=THT]  # not connected
  S56 = Taiway 100-SP-X-T1 SPDT Miniature Toggle Switch [part_number=100-SP-X-T1-0-0-B1-M2 package=THT]  # not connected
  S57 = Taiway 100-SP-X-T1 SPDT Miniature Toggle Switch [part_number=100-SP-X-T1-0-0-B1-M2 package=THT]  # not connected
  S58 = Taiway 100-SP-X-T1 SPDT Miniature Toggle Switch [part_number=100-SP-X-T1-0-0-B1-M2 package=THT]  # not connected
  S59 = Taiway 100-SP-X-T1 SPDT Miniature Toggle Switch [part_number=100-SP-X-T1-0-0-B1-M2 package=THT]  # not connected
  S60 = Momentary Switch [package=ksa_sealed_tac_switch]  # not connected
  S61 = Taiway 100-SP-X-T1 SPDT Miniature Toggle Switch [part_number=100-SP-X-T1-0-0-B1-M2 package=THT]  # not connected
  S62 = Taiway 100-SP-X-T1 SPDT Miniature Toggle Switch [part_number=100-SP-X-T1-0-0-B1-M2 package=THT]  # not connected
  S63 = Taiway 100-SP-X-T1 SPDT Miniature Toggle Switch [part_number=100-SP-X-T1-0-0-B1-M2 package=THT]  # not connected
  S64 = Taiway 100-SP-X-T1 SPDT Miniature Toggle Switch [part_number=100-SP-X-T1-0-0-B1-M2 package=THT]  # not connected
  S65 = Taiway 100-SP-X-T1 SPDT Miniature Toggle Switch [part_number=100-SP-X-T1-0-0-B1-M2 package=THT]  # not connected
  S66 = Taiway 100-SP-X-T1 SPDT Miniature Toggle Switch [part_number=100-SP-X-T1-0-0-B1-M2 package=THT]  # not connected
  S67 = Taiway 100-SP-X-T1 SPDT Miniature Toggle Switch [part_number=100-SP-X-T1-0-0-B1-M2 package=THT]  # not connected
  LED64 = LED - 5mm [color="Orange (620nm)" current=0.030 package="5 mm [THT]"]  # not connected
  LED65 = LED - 5mm [color="Orange (620nm)" current=0.030 package="5 mm [THT]"]  # not connected
  LED66 = LED - 5mm [color="Orange (620nm)" current=0.030 package="5 mm [THT]"]  # not connected
  LED67 = LED - 5mm [color="White (6500K)" current=0.030 package="5 mm [THT]"]  # not connected
  LED68 = LED - 5mm [color="White (6500K)" current=0.030 package="5 mm [THT]"]  # not connected
  LED69 = LED - 5mm [color="White (6500K)" current=0.030 package="5 mm [THT]"]  # not connected
  LED70 = LED - 5mm [color="White (6500K)" current=0.030 package="5 mm [THT]"]  # not connected
  LED71 = LED - 5mm [color="White (6500K)" current=0.030 package="5 mm [THT]"]  # not connected
  LED72 = LED - 5mm [color="White (6500K)" current=0.030 package="5 mm [THT]"]  # not connected
  LED73 = LED - 5mm [color="Orange (620nm)" current=0.030 package="5 mm [THT]"]  # not connected
  LED74 = LED - 5mm [color="Orange (620nm)" current=0.030 package="5 mm [THT]"]  # not connected
  LED75 = LED - 5mm [color="Orange (620nm)" current=0.030 package="5 mm [THT]"]  # not connected
  LED76 = LED - 5mm [color="Orange (620nm)" current=0.030 package="5 mm [THT]"]  # not connected
  LED77 = LED - 5mm [color="Orange (620nm)" current=0.030 package="5 mm [THT]"]  # not connected
  LED78 = LED - 5mm [color="Orange (620nm)" current=0.030 package="5 mm [THT]"]  # not connected
  LED79 = LED - 5mm [color="Orange (620nm)" current=0.030 package="5 mm [THT]"]  # not connected
  LED80 = LED - 5mm [color="Orange (620nm)" current=0.030 package="5 mm [THT]"]  # not connected
  LED81 = LED - 5mm [color="Orange (620nm)" current=0.030 package="5 mm [THT]"]  # not connected
  LED83 = LED - 5mm [color="Orange (620nm)" current=0.030 package="5 mm [THT]"]  # not connected
  LED84 = LED - 5mm [color="Orange (620nm)" current=0.030 package="5 mm [THT]"]  # not connected
  LED85 = LED - 5mm [color="Orange (620nm)" current=0.030 package="5 mm [THT]"]  # not connected
  LED86 = LED - 5mm [color="Orange (620nm)" current=0.030 package="5 mm [THT]"]  # not connected
  LED87 = LED - 5mm [color="Orange (620nm)" current=0.030 package="5 mm [THT]"]  # not connected
  LED89 = LED - 5mm [color="Orange (620nm)" current=0.030 package="5 mm [THT]"]  # not connected
  LED90 = LED - 5mm [color="Orange (620nm)" current=0.030 package="5 mm [THT]"]  # not connected
  LED91 = LED - 5mm [color="Orange (620nm)" current=0.030 package="5 mm [THT]"]  # not connected
  LED92 = LED - 5mm [color="Orange (620nm)" current=0.030 package="5 mm [THT]"]  # not connected
  LED93 = LED - 5mm [color="Orange (620nm)" current=0.030 package="5 mm [THT]"]  # not connected
  switch9 = Rotary_Switch_12x1  # not connected
  S68 = Taiway 100-SP-X-T1 SPDT Miniature Toggle Switch [part_number=100-SP-X-T1-0-0-B1-M2 package=THT]  # not connected
  LED94 = LED - 5mm [color="Orange (620nm)" current=0.030 package="5 mm [THT]"]  # not connected
  LED95 = LED - 5mm [color="Orange (620nm)" current=0.030 package="5 mm [THT]"]  # not connected
  LED96 = LED - 5mm [color="Orange (620nm)" current=0.030 package="5 mm [THT]"]  # not connected
  LED97 = LED - 5mm [color="Orange (620nm)" current=0.030 package="5 mm [THT]"]  # not connected
  LED98 = LED - 5mm [color="Orange (620nm)" current=0.030 package="5 mm [THT]"]  # not connected
  LED99 = LED - 5mm [color="Orange (620nm)" current=0.030 package="5 mm [THT]"]  # not connected
  LED100 = LED - 5mm [color="Orange (620nm)" current=0.030 package="5 mm [THT]"]  # not connected
  LED101 = LED - 5mm [color="Orange (620nm)" current=0.030 package="5 mm [THT]"]  # not connected
  LED102 = LED - 5mm [color="Orange (620nm)" current=0.030 package="5 mm [THT]"]  # not connected
  S69 = Taiway 100-SP-X-T1 SPDT Miniature Toggle Switch [part_number=100-SP-X-T1-0-0-B1-M2 package=THT]  # not connected
  S70 = Taiway 100-SP-X-T1 SPDT Miniature Toggle Switch [part_number=100-SP-X-T1-0-0-B1-M2 package=THT]  # not connected
  S71 = Taiway 100-SP-X-T1 SPDT Miniature Toggle Switch [part_number=100-SP-X-T1-0-0-B1-M2 package=THT]  # not connected
  S72 = Taiway 100-SP-X-T1 SPDT Miniature Toggle Switch [part_number=100-SP-X-T1-0-0-B1-M2 package=THT]  # not connected
  S73 = Taiway 100-SP-X-T1 SPDT Miniature Toggle Switch [part_number=100-SP-X-T1-0-0-B1-M2 package=THT]  # not connected
  S74 = Taiway 100-SP-X-T1 SPDT Miniature Toggle Switch [part_number=100-SP-X-T1-0-0-B1-M2 package=THT]  # not connected
  S75 = Taiway 100-SP-X-T1 SPDT Miniature Toggle Switch [part_number=100-SP-X-T1-0-0-B1-M2 package=THT]  # not connected
  S76 = Taiway 100-SP-X-T1 SPDT Miniature Toggle Switch [part_number=100-SP-X-T1-0-0-B1-M2 package=THT]  # not connected
  S77 = Momentary Switch [package=ksa_sealed_tac_switch]  # not connected
  S78 = Momentary Switch [package=ksa_sealed_tac_switch]  # not connected
  switch10 = Rotary_Switch_12x1  # not connected
  switch11 = Rotary_Switch_12x1  # not connected
  switch12 = Rotary_Switch_12x1  # not connected
  LED103 = LED - 5mm [color="Orange (620nm)" current=0.030 package="5 mm [THT]"]  # not connected
  LED104 = LED - 5mm [color="Orange (620nm)" current=0.030 package="5 mm [THT]"]  # not connected
  LED105 = LED - 5mm [color="Green (570nm)" current=0.030 package="5 mm [THT]"]  # not connected
  LED106 = LED - 5mm [color="Green (570nm)" current=0.030 package="5 mm [THT]"]  # not connected
  switch13 = Rotary_Switch_12x1  # not connected
  switch14 = Rotary_Switch_12x1  # not connected
  S79 = Taiway 100-SP-X-T1 SPDT Miniature Toggle Switch [part_number=100-SP-X-T1-0-0-B1-M2 package=THT]  # not connected
  S31 = Momentary Switch [package=ksa_sealed_tac_switch]  # not connected
  S80 = Momentary Switch [package=ksa_sealed_tac_switch]  # not connected
  L2 = Solenoid  # not connected
  L3 = Solenoid  # not connected
  DM13A = MAX7219 [package=dil24]
  GND = STARBOARD_GND [package=starboard_ground_small]
  LED107 = LED - 5mm [color="Orange (620nm)" current=0.030 package="5 mm [THT]"]
  LED108 = LED - 5mm [color="Orange (620nm)" current=0.030 package="5 mm [THT]"]
  GND1 = STARBOARD_GND [package=starboard_ground_small]  # not connected

nets:
  GND: RSC_Master_Board.GND, Mux1.GND, Mux1.EN
  5V: RSC_Master_Board.5V, Mux1.VCC, R1.Pin_0
  N1: RSC_Master_Board.D22, Mux1.S0
  N2: RSC_Master_Board.D23, Mux1.S1
  N3: RSC_Master_Board.D24, Mux1.S2
  N4: RSC_Master_Board.D25, Mux1.S3
  N5: RSC_Master_Board.D38, Mux1.SIG, R1.Pin_1
  N6: Mux3.C0, S9.L2
  N7: Mux3.C1, S9.L1
  N8: Mux4.C0, S1.L1
  N9: Mux4.C1, S1.L2
  N10: Mux4.C2, S2.L1
  N11: Mux4.C3, S2.L2
  N12: Mux4.C4, S3.L2
  N13: Mux4.C5, S4.L1
  N14: Mux4.C6, S4.L2
  N15: Mux4.C7, S24.L2
  N16: Mux4.C8, S5.L2
  N17: Mux4.C9, S5.L1
  N18: Mux4.C10, S6.L2
  N19: Mux4.C11, S6.L1
  N20: Mux4.C12, S7.L2
  N21: Mux4.C13, S7.L1
  N22: Mux4.C14, S8.L2
  N23: Mux4.C15, S8.L1
  N24: S1.COM, S2.COM, S4.COM, S5.COM, S6.COM, S7.COM, S8.COM, S9.COM, S24.L1, GND.MOUNT
  N25: LED1.anode, DM13A.CLK
  N26: LED2.anode, DM13A.SEGA
  N27: LED3.anode, DM13A.SEGF
  N28: LED6.anode, DM13A.VCC
  N29: LED7.anode, DM13A.SEGC
  N30: LED8.anode, DM13A.LOAD
  N31: LED9.anode, DM13A.DIG1
  N32: LED10.anode, DM13A.ISET
  N33: DM13A.SEGB, LED108.anode
  N34: DM13A.SEGG, LED107.anode
